# Fritzing sketch ILEM Schematic (saved by Fritzing 0.9.3b)
breadboards: 1

parts:
  Part1 = Arduino Micro (Rev3)
  Part2 = Logic Level Converter
  Raspberry_Pi_1 = Raspberry Pi 3 [part_number=RPI-3-V1.2]
  Part4 = ws2812b [package="smd 2812b"]

nets:
  GND: Part1.GND, Part2.GND, Raspberry_Pi_1.GND, Part4.VSS
  N1: Part1.D2/SDA, Part2.TX_HV
  N2: Part1.D3/SCL, Part2.RX_HV
  5V: Part1.5V, Raspberry_Pi_1.5V, Part4.VDD
  N3: Part1.D13_PWM, Part4.DIN
  N4: Part2.LV, Raspberry_Pi_1.3v3
  N5: Part2.RX_LV, Raspberry_Pi_1.GPIO3
  N6: Part2.TX_LV, Raspberry_Pi_1.GPIO2
